# Fritzing sketch pulse2dtmf (saved by Fritzing 0.9.6b)
circuit board: 2cm x 4.3cm
breadboards: 1

parts:
  P = Header 1 [package=1x01_offset]
  C3 = Ceramic Capacitor [capacitance=100nF voltage=35V package="100 mil [THT, multilayer]"]
  C4 = Ceramic Capacitor [capacitance=100nF voltage=35V package="100 mil [THT, multilayer]"]
  ATTINY85 = attiny85 [package=dip]
  D1 = DIODE-ZENER [package=diode-zener]
  L+ = Header 1 [package=1x01_offset]
  G = Header 1 [package=1x01_offset]
  C1 = Ceramic Capacitor [capacitance=100nF voltage=35V package="100 mil [THT, multilayer]"]
  C6 = Ceramic Capacitor [capacitance=22pF voltage=35V package="100 mil [THT, multilayer]"]
  Y1 = Crystal [frequency="4 MHz" package=THT]
  R1 = Resistor [tolerance=±5% power=0.25 resistance=680 package=THT]
  D = Header 1 [package=1x01_offset]
  C2 = Ceramic Capacitor [capacitance=100nF voltage=35V package="100 mil [THT, multilayer]"]
  C5 = Ceramic Capacitor [capacitance=22pF voltage=35V package="100 mil [THT, multilayer]"]
  LM78L05 = Voltage Regulator [package=to-92]

nets:
  N1: P.1, C4.1, ATTINY85.Pin_7
  GND: C3.0, C4.0, ATTINY85.Pin_4, D1.A, G.1, C1.0, C6.0, R1.Pin_1, C2.0, C5.0, LM78L05.GND
  N2: C3.1, ATTINY85.Pin_6, D.1
  N3: ATTINY85.Pin_2, Y1.pin_0, C5.1
  N4: ATTINY85.Pin_3, C6.1, Y1.pin_1
  N5: ATTINY85.Pin_5, R1.Pin_0
  N6: ATTINY85.Pin_8, C2.1, LM78L05.OUT
  N7: D1.C, L+.1, C1.1, LM78L05.IN

custom parts:
  Voltage Regulator: Voltage Regulator Standard 7805 5V regulator. IGO (Input Ground Output). Spark Fun Electronics SKU : COM-00107
